# Fritzing sketch thermostat_sketch (saved by Fritzing 0.9.3b)
breadboards: 1

parts:
  WeMos_D1_Mini1 = WeMos D1 Mini
  WeMos_D1_Mini_Relay_Shield_V1 = WeMos D1 Mini Relay Shield V2
  WeMos_D1_Mini_OLED_Shield1 = WeMos D1 Mini OLED Shield
  HLK-PM1 = HLK-PM01
  R2 = Resistor [tolerance=±5% resistance=10 package="0805 [SMD]"]
  R1 = Resistor [tolerance=±5% resistance=68 package="0805 [SMD]"]
  Součástka1 = Humidity Temperature Sensor SHT15
  LED1 = RGB LED (com. anode, rbg) [color="Red (633nm)" package="5 mm [THT]"]

nets:
  3V3: WeMos_D1_Mini1.3V3, WeMos_D1_Mini_OLED_Shield1.3V3, Součástka1.VCC
  5V: WeMos_D1_Mini1.5V, WeMos_D1_Mini_Relay_Shield_V1.5V, HLK-PM1.+Vo
  N1: WeMos_D1_Mini1.D1, WeMos_D1_Mini_OLED_Shield1.D1
  N2: WeMos_D1_Mini1.D2, WeMos_D1_Mini_OLED_Shield1.D2, Součástka1.SDA
  N3: WeMos_D1_Mini1.D4, WeMos_D1_Mini_Relay_Shield_V1.D1
  N4: WeMos_D1_Mini1.D6, R1.Pin_1
  N5: WeMos_D1_Mini1.D7, R2.Pin_0
  N6: WeMos_D1_Mini1.G, WeMos_D1_Mini_Relay_Shield_V1.G, WeMos_D1_Mini_OLED_Shield1.G, HLK-PM1.-Vo
  N7: R2.Pin_1, LED1.green_cathode
  N8: R1.Pin_0, LED1.red_cathode

notes:
  220V
  Thermostat 220V/2A
  Normally open
  SHT3X
  3V3 -> VIN
  G -> GND
  D1 -> SLC/T
  D2 -> SAA/RH
  RGB LED, common anode
  D6 -> Red
  D7 -> Green
  D8 -> Blue
  3.3V -> Anode
